// Logisim project Somador.circ as structural Verilog: 1 circuit, main circuit main
module main (
  input  A,
  input  B,
  input  C,
  output Sn,
  output Cout
);

  wire and_1_out, and_2_out, and_3_out;

  and and_1 (and_1_out, A, B);
  and and_2 (and_2_out, A, C);
  and and_3 (and_3_out, B, C);
  ExactlyOne xor_1 (.out(Sn), .in0(A), .in1(B), .in2(C));
  or or_1 (Cout, and_1_out, and_2_out, and_3_out);
endmodule
