// Logisim project Somador8bits.circ as structural Verilog: 1 circuit, main circuit main
module main (
  input  a0,
  input  a0_2,
  input  a0_3,
  input  a0_4,
  input  a0_5,
  input  a0_6,
  input  a0_7,
  input  a0_8,
  input  cin,
  input  b0,
  input  b0_2,
  input  b0_3,
  input  b0_4,
  input  b0_5,
  input  b0_6,
  input  b0_7,
  input  b0_8,
  output out_18,
  output out_19,
  output out_20,
  output out_21,
  output out_22,
  output out_23,
  output out_24,
  output out_25,
  output out_26
);

  wire and_1_out, and_2_out, and_3_out, and_4_out, and_5_out, and_6_out, and_7_out, and_8_out, and_9_out,
       and_10_out, and_11_out, and_12_out, and_13_out, and_14_out, and_15_out, and_16_out, and_17_out,
       and_18_out, and_19_out, and_20_out, and_21_out, and_22_out, and_23_out, and_24_out, or_2_out,
       or_3_out, or_4_out, or_5_out, or_6_out, or_7_out, or_8_out;

  or or_1 (out_26, and_1_out, and_2_out, and_3_out);
  ExactlyOne xor_1 (.out(out_25), .in0(a0_8), .in1(or_2_out), .in2(b0_8));
  and and_1 (and_1_out, a0_8, or_2_out);
  and and_2 (and_2_out, a0_8, b0_8);
  and and_3 (and_3_out, or_2_out, b0_8);
  or or_2 (or_2_out, and_4_out, and_5_out, and_6_out);
  ExactlyOne xor_2 (.out(out_24), .in0(a0_7), .in1(or_3_out), .in2(b0_7));
  and and_4 (and_4_out, a0_7, or_3_out);
  and and_5 (and_5_out, a0_7, b0_7);
  and and_6 (and_6_out, or_3_out, b0_7);
  or or_3 (or_3_out, and_7_out, and_8_out, and_9_out);
  ExactlyOne xor_3 (.out(out_23), .in0(a0_6), .in1(or_4_out), .in2(b0_6));
  and and_7 (and_7_out, a0_6, or_4_out);
  and and_8 (and_8_out, a0_6, b0_6);
  and and_9 (and_9_out, or_4_out, b0_6);
  or or_4 (or_4_out, and_10_out, and_11_out, and_12_out);
  ExactlyOne xor_4 (.out(out_22), .in0(a0_5), .in1(or_5_out), .in2(b0_5));
  and and_10 (and_10_out, a0_5, or_5_out);
  and and_11 (and_11_out, a0_5, b0_5);
  and and_12 (and_12_out, or_5_out, b0_5);
  or or_5 (or_5_out, and_13_out, and_14_out, and_15_out);
  ExactlyOne xor_5 (.out(out_21), .in0(a0_4), .in1(or_6_out), .in2(b0_4));
  and and_13 (and_13_out, a0_4, or_6_out);
  and and_14 (and_14_out, a0_4, b0_4);
  and and_15 (and_15_out, or_6_out, b0_4);
  or or_6 (or_6_out, and_16_out, and_17_out, and_18_out);
  ExactlyOne xor_6 (.out(out_20), .in0(a0_3), .in1(or_7_out), .in2(b0_3));
  and and_16 (and_16_out, a0_3, or_7_out);
  and and_17 (and_17_out, a0_3, b0_3);
  and and_18 (and_18_out, or_7_out, b0_3);
  or or_7 (or_7_out, and_19_out, and_20_out, and_21_out);
  ExactlyOne xor_7 (.out(out_19), .in0(a0_2), .in1(or_8_out), .in2(b0_2));
  and and_19 (and_19_out, a0_2, or_8_out);
  and and_20 (and_20_out, a0_2, b0_2);
  and and_21 (and_21_out, or_8_out, b0_2);
  or or_8 (or_8_out, and_22_out, and_23_out, and_24_out);
  ExactlyOne xor_8 (.out(out_18), .in0(a0), .in1(cin), .in2(b0));
  and and_22 (and_22_out, a0, cin);
  and and_23 (and_23_out, a0, b0);
  and and_24 (and_24_out, cin, b0);
endmodule
