// Logisim project Subtrator.circ as structural Verilog: 1 circuit, main circuit main
module main (
  input  A,
  input  B,
  input  C,
  output Sn,
  output Cout
);

  wire and_1_out, and_2_out, and_3_out, not_1_out;

  ExactlyOne xor_1 (.out(Sn), .in0(A), .in1(B), .in2(C));
  not not_1 (not_1_out, A);
  and and_1 (and_1_out, not_1_out, B);
  and and_2 (and_2_out, not_1_out, C);
  and and_3 (and_3_out, B, C);
  or or_1 (Cout, and_1_out, and_2_out, and_3_out);
endmodule
