// Logisim project Subtrator3bits.circ as structural Verilog: 1 circuit, main circuit main
module main (
  input  a0,
  input  a0_2,
  input  a0_3,
  input  cin,
  input  b0,
  input  b0_2,
  input  b0_3,
  output out_8,
  output out_9,
  output out_10,
  output out_11
);

  wire and_1_out, and_2_out, and_3_out, and_4_out, and_5_out, and_6_out, and_7_out, and_8_out, and_9_out,
       not_1_out, not_2_out, not_3_out, or_2_out, or_3_out;

  or or_1 (out_11, and_1_out, and_2_out, and_3_out);
  and and_1 (and_1_out, not_1_out, or_2_out);
  and and_2 (and_2_out, not_1_out, b0_3);
  and and_3 (and_3_out, or_2_out, b0_3);
  ExactlyOne xor_1 (.out(out_10), .in0(a0_3), .in1(or_2_out), .in2(b0_3));
  not not_1 (not_1_out, a0_3);
  or or_2 (or_2_out, and_4_out, and_5_out, and_6_out);
  and and_4 (and_4_out, not_2_out, or_3_out);
  and and_5 (and_5_out, not_2_out, b0_2);
  and and_6 (and_6_out, or_3_out, b0_2);
  ExactlyOne xor_2 (.out(out_9), .in0(a0_2), .in1(or_3_out), .in2(b0_2));
  not not_2 (not_2_out, a0_2);
  or or_3 (or_3_out, and_7_out, and_8_out, and_9_out);
  and and_7 (and_7_out, not_3_out, cin);
  and and_8 (and_8_out, not_3_out, b0);
  and and_9 (and_9_out, cin, b0);
  not not_3 (not_3_out, a0);
  ExactlyOne xor_3 (.out(out_8), .in0(a0), .in1(cin), .in2(b0));
endmodule
