// Logisim project BCD8421-Excesso3.circ as structural Verilog: 1 circuit, main circuit main
module main (
  input  A,
  input  B,
  input  C,
  input  D,
  output S3,
  output S2,
  output S1,
  output S0
);

  wire and_1_out, and_2_out, and_3_out, and_4_out, and_5_out, not_1_out, not_2_out, not_3_out, not_4_out;

  and and_1 (and_1_out, B, D);
  and and_2 (and_2_out, B, C);
  not not_1 (not_1_out, B);
  not not_2 (not_2_out, B);
  not not_3 (not_3_out, C);
  not not_4 (not_4_out, D);
  xnor xnor_1 (S1, C, D);
  not not_5 (S0, D);
  or or_1 (S3, and_1_out, and_2_out, A);
  and and_3 (and_3_out, not_1_out, D);
  and and_4 (and_4_out, not_2_out, C);
  and and_5 (and_5_out, B, not_3_out, not_4_out);
  or or_2 (S2, and_3_out, and_4_out, and_5_out);
endmodule
