// Logisim project Flip-Flop-D.circ as structural Verilog: 1 circuit, main circuit main
module main (
  input  D,
  input  in_2,
  output Q,
  output Q_prime
);

  wire and_1_out, and_2_out, CLOCK_out, not_1_out;

  not not_1 (not_1_out, D);
  Clock CLOCK (.out(CLOCK_out));
  and and_1 (and_1_out, Q, D, CLOCK_out);
  and and_2 (and_2_out, CLOCK_out, not_1_out, Q_prime);
  nor nor_1 (Q, and_1_out, in_2, Q_prime);
  nor nor_2 (Q_prime, Q, in_2, and_2_out);
endmodule
