// Logisim project Flip-Flop-JK.circ as structural Verilog: 2 circuits, main circuit main
module main (
  input  K,
  input  in_2,
  input  J,
  output Q,
  output Q_prime
);

  wire and_1_out, and_2_out, CLOCK_out;

  Clock CLOCK (.out(CLOCK_out));
  and and_1 (and_1_out, Q, K, CLOCK_out);
  and and_2 (and_2_out, CLOCK_out, J, Q_prime);
  nor nor_1 (Q, and_1_out, in_2, Q_prime);
  nor nor_2 (Q_prime, Q, in_2, and_2_out);
endmodule

module teste (
);

  main main_1 ();  // open: K, in_2, J, Q, Q_prime
endmodule
