// Logisim project Flip-Flop-T.circ as structural Verilog: 1 circuit, main circuit main
module main (
  input  T,
  input  in_2,
  output Q,
  output Q_prime
);

  wire and_1_out, and_2_out, CLOCK_out;

  Clock CLOCK (.out(CLOCK_out));
  and and_1 (and_1_out, Q, T, CLOCK_out);
  and and_2 (and_2_out, CLOCK_out, T, Q_prime);
  nor nor_1 (Q, and_1_out, in_2, Q_prime);
  nor nor_2 (Q_prime, Q, in_2, and_2_out);
endmodule
