// Logisim project Latches.circ as structural Verilog: 1 circuit, main circuit main
module main (
  input  SET,
  input  RESET,
  output Qa,
  output Qf
);

  nand nand_1 (Qa, SET, Qf);
  nand nand_2 (Qf, Qa, RESET);
endmodule
