// Logisim project DEMUX-8bits.circ as structural Verilog: 2 circuits, main circuit main
module main (
  input  S1,
  input  S2,
  input  S3,
  input  S4,
  input  C2,
  input  C3,
  input  in_7,
  input  C1,
  input  S5,
  input  S6,
  input  S7,
  input  S8,
  input  C2_2,
  input  C3_2
);

  wire demux_1_s1, demux_1_s4;

  DEMUX demux_1 (.I(in_7), .C1(C1), .C2(C1), .S1(demux_1_s1), .S4(demux_1_s4));  // open: S2, S3
  DEMUX demux_2 (.I(demux_1_s1), .C1(C2), .C2(C3), .S1(S1), .S2(S2), .S3(S3), .S4(S4));
  DEMUX demux_3 (.I(demux_1_s4), .C1(C2_2), .C2(C3_2), .S1(S5), .S2(S6), .S3(S7), .S4(S8));
endmodule

module DEMUX (
  input  I,
  input  C1,
  input  C2,
  output S1,
  output S2,
  output S3,
  output S4
);

  wire and_1_out, and_2_out, and_3_out, and_4_out, not_1_out, not_2_out, not_3_out, not_4_out;

  not not_1 (not_1_out, C2);
  assign S1 = and_1_out ? I : 1'bz;  // Controlled_Buffer controlled_buffer_1
  and and_1 (and_1_out, not_1_out, not_2_out);
  and and_2 (and_2_out, C2, not_4_out);
  not not_2 (not_2_out, C1);
  assign S2 = and_2_out ? I : 1'bz;  // Controlled_Buffer controlled_buffer_2
  assign S3 = and_3_out ? I : 1'bz;  // Controlled_Buffer controlled_buffer_3
  and and_3 (and_3_out, not_3_out, C1);
  not not_3 (not_3_out, C2);
  not not_4 (not_4_out, C1);
  assign S4 = and_4_out ? I : 1'bz;  // Controlled_Buffer controlled_buffer_4
  and and_4 (and_4_out, C2, C1);
endmodule
