// Logisim project DEMUX_via_Buffers_3-State.circ as structural Verilog: 1 circuit, main circuit main
module main (
  input  I,
  input  C1,
  input  C2,
  output S1,
  output S2,
  output S3,
  output S4
);

  wire and_1_out, and_2_out, and_3_out, and_4_out, not_1_out, not_2_out, not_3_out, not_4_out;

  not not_1 (not_1_out, C2);
  assign S1 = and_2_out ? I : 1'bz;  // Controlled_Buffer controlled_buffer_1
  and and_1 (and_1_out, C2, not_3_out);
  and and_2 (and_2_out, not_1_out, not_2_out);
  not not_2 (not_2_out, C1);
  assign S2 = and_1_out ? I : 1'bz;  // Controlled_Buffer controlled_buffer_2
  assign S3 = and_3_out ? I : 1'bz;  // Controlled_Buffer controlled_buffer_3
  and and_3 (and_3_out, not_4_out, C1);
  not not_3 (not_3_out, C1);
  not not_4 (not_4_out, C2);
  assign S4 = and_4_out ? I : 1'bz;  // Controlled_Buffer controlled_buffer_4
  and and_4 (and_4_out, C2, C1);
endmodule
