// Logisim project MUX-8bits.circ as structural Verilog: 2 circuits, main circuit main
module main (
  input  I1,
  input  I2,
  input  C2,
  input  I3,
  input  C3,
  input  C1,
  input  I4,
  input  I5,
  input  I6,
  input  C2_2,
  input  I7,
  input  C3_2,
  input  I8,
  output S
);

  wire mux_4_1_out_7, mux_4_2_out_7, undriven, undriven_2;

  MUX_4 mux_4_1 (.A(I4), .B(I3), .C(I2), .D(I1), .C1(C3), .C2(C2), .out_7(mux_4_1_out_7));
  MUX_4 mux_4_2 (.A(I8), .B(I7), .C(I6), .D(I5), .C1(C3_2), .C2(C2_2), .out_7(mux_4_2_out_7));
  MUX_4 mux_4_3 (.A(mux_4_2_out_7), .B(undriven_2), .C(undriven), .D(mux_4_1_out_7), .C1(C1), .C2(C1), .out_7(S));
endmodule

module MUX_4 (
  input  A,
  input  B,
  input  C,
  input  D,
  input  C1,
  input  C2,
  output out_7
);

  wire and_1_out, and_2_out, and_3_out, and_4_out, not_1_out, not_2_out, not_3_out, not_4_out;

  not not_1 (not_1_out, C2);
  assign out_7 = and_1_out ? A : 1'bz;  // Controlled_Buffer controlled_buffer_1
  and and_1 (and_1_out, not_1_out, not_2_out);
  not not_2 (not_2_out, C1);
  assign out_7 = and_2_out ? B : 1'bz;  // Controlled_Buffer controlled_buffer_2
  and and_2 (and_2_out, C2, not_3_out);
  and and_3 (and_3_out, not_4_out, C1);
  not not_3 (not_3_out, C1);
  not not_4 (not_4_out, C2);
  assign out_7 = and_3_out ? C : 1'bz;  // Controlled_Buffer controlled_buffer_3
  assign out_7 = and_4_out ? D : 1'bz;  // Controlled_Buffer controlled_buffer_4
  and and_4 (and_4_out, C2, C1);
endmodule
