// Logisim project MUX_via_Buffers_3-State.circ as structural Verilog: 1 circuit, main circuit main
module main (
  input  A,
  input  B,
  input  C,
  input  D,
  input  C1,
  input  C2,
  output out_7
);

  wire and_1_out, and_2_out, and_3_out, and_4_out, not_1_out, not_2_out, not_3_out, not_4_out;

  not not_1 (not_1_out, C2);
  assign out_7 = and_1_out ? A : 1'bz;  // Controlled_Buffer controlled_buffer_1
  and and_1 (and_1_out, not_1_out, not_2_out);
  not not_2 (not_2_out, C1);
  assign out_7 = and_2_out ? B : 1'bz;  // Controlled_Buffer controlled_buffer_2
  and and_2 (and_2_out, C2, not_4_out);
  and and_3 (and_3_out, not_3_out, C1);
  not not_3 (not_3_out, C2);
  not not_4 (not_4_out, C1);
  assign out_7 = and_3_out ? C : 1'bz;  // Controlled_Buffer controlled_buffer_3
  assign out_7 = and_4_out ? D : 1'bz;  // Controlled_Buffer controlled_buffer_4
  and and_4 (and_4_out, C2, C1);
endmodule
