// Logisim project Paralelo-Serie.circ as structural Verilog: 1 circuit, main circuit main
module main (
  input  Clear,
  input  ENABLE,
  input  d7,
  input  d6,
  input  d5,
  input  d4,
  input  d3,
  input  d2,
  input  d1,
  input  d0,
  output \SAÍDA 
);

  wire and_1_out, and_2_out, and_3_out, and_4_out, and_5_out, and_6_out, and_7_out, and_8_out, Clock_out,
       d_ff_1_q, d_ff_2_q, d_ff_3_q, d_ff_4_q, d_ff_5_q, d_ff_6_q, d_ff_7_q;

  Clock Clock (.out(Clock_out));
  D_Flip_Flop d_ff_1 (.clk(Clock_out), .D(1'b0), .Q(d_ff_1_q), .preset(and_1_out), .reset(Clear));  // open: Qn, en
  and and_1 (and_1_out, ENABLE, d7);
  and and_2 (and_2_out, ENABLE, d6);
  D_Flip_Flop d_ff_2 (.clk(Clock_out), .D(d_ff_1_q), .Q(d_ff_2_q), .preset(and_2_out), .reset(Clear));  // open: Qn, en
  D_Flip_Flop d_ff_3 (.clk(Clock_out), .D(d_ff_2_q), .Q(d_ff_3_q), .preset(and_3_out), .reset(Clear));  // open: Qn, en
  and and_3 (and_3_out, ENABLE, d5);
  and and_4 (and_4_out, ENABLE, d4);
  D_Flip_Flop d_ff_4 (.clk(Clock_out), .D(d_ff_3_q), .Q(d_ff_4_q), .preset(and_4_out), .reset(Clear));  // open: Qn, en
  D_Flip_Flop d_ff_5 (.clk(Clock_out), .D(d_ff_4_q), .Q(d_ff_5_q), .preset(and_5_out), .reset(Clear));  // open: Qn, en
  and and_5 (and_5_out, ENABLE, d3);
  D_Flip_Flop d_ff_6 (.clk(Clock_out), .D(d_ff_5_q), .Q(d_ff_6_q), .preset(and_6_out), .reset(Clear));  // open: Qn, en
  and and_6 (and_6_out, ENABLE, d2);
  and and_7 (and_7_out, ENABLE, d1);
  D_Flip_Flop d_ff_7 (.clk(Clock_out), .D(d_ff_6_q), .Q(d_ff_7_q), .preset(and_7_out), .reset(Clear));  // open: Qn, en
  and and_8 (and_8_out, ENABLE, d0);
  D_Flip_Flop d_ff_8 (.clk(Clock_out), .D(d_ff_7_q), .Q(\SAÍDA ), .preset(and_8_out), .reset(Clear));  // open: Qn, en
endmodule
